# Fritzing sketch adc_board_final (saved by Fritzing 0.8.7b)
circuit board: 6.28529cm x 4.96564cm
breadboards: 1

parts:
  R1 = Resistor [tolerance=±5% resistance=33 package=THT]
  R2 = Resistor [tolerance=±5% resistance=33 package=THT]
  R3 = Resistor [tolerance=±5% resistance=33 package=THT]
  R4 = Resistor [tolerance=±5% resistance=33 package=THT]
  R5 = Resistor [tolerance=±5% resistance=33 package=THT]
  R6 = Resistor [tolerance=±5% resistance=33 package=THT]
  R7 = Resistor [tolerance=±5% resistance=33 package=THT]
  R8 = Resistor [tolerance=±5% resistance=33 package=THT]
  IC1 = IC, DIP package, 8 pins [chip_label=IC]
  ADC = IC, DIP package, 16 pins [chip_label=IC]
  C1 = Ceramic Capacitor [capacitance=100nF package="100 mil [THT, multilayer]"]
  C2 = Ceramic Capacitor [capacitance=100nF package="100 mil [THT, multilayer]"]
  C3 = Ceramic Capacitor [capacitance=100nF package="100 mil [THT, multilayer]"]
  C4 = Ceramic Capacitor [capacitance=100nF package="100 mil [THT, multilayer]"]
  C5 = Ceramic Capacitor [capacitance=100nF package="100 mil [THT, multilayer]"]
  C6 = Ceramic Capacitor [capacitance=100nF package="100 mil [THT, multilayer]"]
  C7 = Ceramic Capacitor [capacitance=100nF package="100 mil [THT, multilayer]"]
  C8 = Ceramic Capacitor [capacitance=100nF package="100 mil [THT, multilayer]"]
  IC2 = IC, DIP package, 8 pins [chip_label=IC]
  IC3 = IC, DIP package, 8 pins [chip_label=IC]
  IC4 = IC, DIP package, 8 pins [chip_label=IC]
  C10 = Ceramic Capacitor [capacitance=0.1µF package="100 mil [THT, multilayer]"]
  C11 = Ceramic Capacitor [capacitance=1µF package="100 mil [THT, multilayer]"]
  C9 = Ceramic Capacitor [capacitance=10µF package="100 mil [THT, multilayer]"]
  REF = IC, DIP package, 8 pins [chip_label=IC]
  C12 = Ceramic Capacitor [capacitance=1µF package="100 mil [THT, multilayer]"]
  SPI = screw terminal, 4 pins
  LED = LED - 3mm [color="Red (633nm)" package="3 mm [THT]"]
  R9 = Resistor [tolerance=±5% resistance=220 package=THT]
  12V = Screw terminal - 2 pins [package=THT]
  R10 = Resistor [tolerance=±5% resistance=0 package="1206 [SMD]"]
  5V = Screw terminal - 2 pins [package=THT]
  TRIM = IC, SIP package, 3 pins [chip_label=IC]
  CH0 = screw terminal, 3 pins
  CH1 = screw terminal, 3 pins
  CH2 = screw terminal, 3 pins
  CH3 = screw terminal, 3 pins
  CH4 = screw terminal, 3 pins
  CH6 = screw terminal, 3 pins
  CH7 = screw terminal, 3 pins
  CH5 = screw terminal, 3 pins
  DC/DC = IC, SIP package, 3 pins [chip_label=IC]

nets:
  N1: R1.Pin_0, IC1.pin1, IC1.pin2
  N2: R1.Pin_1, ADC.pin1, C1.1
  N3: R2.Pin_0, IC1.pin6, IC1.pin7
  N4: R2.Pin_1, ADC.pin2, C2.0
  N5: R3.Pin_0, IC2.pin1, IC2.pin2
  N6: R3.Pin_1, ADC.pin3, C3.1
  N7: R4.Pin_0, IC2.pin6, IC2.pin7
  N8: R4.Pin_1, ADC.pin4, C4.0
  N9: R5.Pin_0, IC3.pin1, IC3.pin2
  N10: R5.Pin_1, ADC.pin5, C5.1
  N11: R6.Pin_0, IC3.pin6, IC3.pin7
  N12: R6.Pin_1, ADC.pin6, C6.0
  N13: R7.Pin_0, IC4.pin1, IC4.pin2
  N14: R7.Pin_1, ADC.pin7, C7.1
  N15: R8.Pin_0, IC4.pin6, IC4.pin7
  N16: R8.Pin_1, ADC.pin8, C8.0
  N17: IC1.pin3, CH0.pin1
  GND: IC1.pin4, ADC.pin9, ADC.pin14, C1.0, C2.1, C3.0, C4.1, C5.0, C6.1, C7.0, C8.1, IC2.pin4, IC3.pin4, IC4.pin4, C10.1, C11.0, C9.0, REF.pin4, C12.0, R9.Pin_0, 12V.pin2, 5V.pin2, TRIM.pin1, CH0.pin2, CH1.pin2, CH2.pin2, CH3.pin2, CH4.pin2, CH6.pin2, CH7.pin2, CH5.pin2, DC/DC.pin2
  N18: IC1.pin5, CH1.pin1
  5V: IC1.pin8, ADC.pin16, IC2.pin8, IC3.pin8, IC4.pin8, C10.0, C9.1, LED.anode, R10.Pin_1, 5V.pin1, CH0.pin3, CH1.pin3, CH2.pin3, CH3.pin3, CH4.pin3, CH6.pin3, CH7.pin3, CH5.pin3, DC/DC.pin3
  N19: ADC.pin10, SPI.pin4
  N20: ADC.pin11, SPI.pin3
  N21: ADC.pin12, SPI.pin2
  N22: ADC.pin13, SPI.pin1
  Vref: ADC.pin15, C11.1, REF.pin6, R10.Pin_0, TRIM.pin3
  N23: IC2.pin3, CH2.pin1
  N24: IC2.pin5, CH3.pin1
  N25: IC3.pin3, CH4.pin1
  N26: IC3.pin5, CH5.pin1
  N27: IC4.pin3, CH6.pin1
  N28: IC4.pin5, CH7.pin1
  Vin: REF.pin2, C12.1, 12V.pin1, DC/DC.pin1
  N29: REF.pin5, TRIM.pin2
  N30: LED.cathode, R9.Pin_1

notes:
  ADC
  Nessie
  Arnau
  June'14
  Warning!
  (OSL)
  PCB
  Shorting this bypass you are
  connecting directly the Vref to 5V
  in case you don't want to use IC6
  +
  Bypass REF
